// Logisim project G0401a.circ as structural Verilog: 1 circuit, main circuit main
module main (
  input  X,
  input  Y,
  input  Z,
  output out_4
);

  wire not_1_out, not_2_out, not_3_out, or_1_out;

  not not_1 (not_1_out, X);
  and and_1 (out_4, not_1_out, not_3_out);
  not not_2 (not_2_out, Y);
  or or_1 (or_1_out, not_2_out, Z);
  not not_3 (not_3_out, or_1_out);
endmodule
