// Logisim project G0401d.circ as structural Verilog: 1 circuit, main circuit main
module main (
  input  X,
  input  Y,
  input  Z,
  output out_4
);

  wire and_1_out, not_1_out, not_2_out;

  not not_1 (not_1_out, X);
  and and_1 (and_1_out, not_1_out, Y);
  not not_2 (not_2_out, and_1_out);
  and and_2 (out_4, not_2_out, Z);
endmodule
