// Logisim project G07.circ as structural Verilog: 7 circuits, main circuit G0701
module G0701 (
  input  x,
  input  y,
  input  _0___and_1___nand,
  input  x_2,
  input  y_2,
  output s,
  output s1,
  output s2
);

  wire and_1_out, and_3_out, and_4_out, nand_1_out, not_1_out;

  and and_1 (and_1_out, x, y);
  not not_1 (not_1_out, _0___and_1___nand);
  nand nand_1 (nand_1_out, y, x);
  and and_2 (s1, x_2, y_2);
  nand nand_2 (s2, y_2, x_2);
  and and_3 (and_3_out, and_1_out, not_1_out);
  and and_4 (and_4_out, nand_1_out, _0___and_1___nand);
  or or_1 (s, and_3_out, and_4_out);
endmodule

module G0702 (
  input  x,
  input  y,
  input  _0_or_1_nor,
  output s
);

  wire and_1_out, and_2_out, nor_1_out, not_1_out, or_1_out;

  or or_1 (or_1_out, x, y);
  not not_1 (not_1_out, _0_or_1_nor);
  nor nor_1 (nor_1_out, y, x);
  and and_1 (and_1_out, or_1_out, not_1_out);
  and and_2 (and_2_out, nor_1_out, _0_or_1_nor);
  or or_2 (s, and_1_out, and_2_out);
endmodule

module G0703 (
  input  x,
  input  y,
  input  _0___or_nor_1__and_nand,
  input  _0___normal_1___not,
  output s
);

  wire and_1_out, and_2_out, and_3_out, and_4_out, and_5_out, and_6_out, and_7_out, and_8_out, and_9_out,
       nand_1_out, nor_1_out, not_1_out, not_2_out, not_3_out, not_4_out, or_1_out;

  or or_1 (or_1_out, x, y);
  nor nor_1 (nor_1_out, x, y);
  not not_1 (not_1_out, _0___or_nor_1__and_nand);
  and and_1 (and_1_out, x, y);
  nand nand_1 (nand_1_out, x, y);
  and and_2 (and_2_out, or_1_out, not_1_out);
  not not_2 (not_2_out, not_3_out);
  and and_3 (and_3_out, nor_1_out, not_1_out);
  not not_3 (not_3_out, not_4_out);
  and and_4 (and_4_out, and_1_out, _0___or_nor_1__and_nand);
  not not_4 (not_4_out, _0___normal_1___not);
  and and_5 (and_5_out, nand_1_out, _0___or_nor_1__and_nand);
  and and_6 (and_6_out, and_2_out, not_2_out);
  and and_7 (and_7_out, and_3_out, not_3_out);
  or or_2 (s, and_6_out, and_7_out, and_8_out, and_9_out);
  and and_8 (and_8_out, and_4_out, not_4_out);
  and and_9 (and_9_out, and_5_out, _0___normal_1___not);
endmodule

module G0704 (
  input  x,
  input  y,
  input  [1:0] _00___or___01___nor___10___xor___11___xnor,
  output s
);

  wire and_1_out, and_2_out, and_3_out, and_4_out, and_5_out, and_6_out, and_7_out, and_8_out, nor_1_out,
       not_1_out, not_2_out, not_3_out, not_4_out, or_1_out, xnor_1_out, xor_1_out;

  or or_1 (or_1_out, x, y);
  nor nor_1 (nor_1_out, x, y);
  not not_1 (not_1_out, _00___or___01___nor___10___xor___11___xnor[1]);
  xor xor_1 (xor_1_out, x, y);
  xnor xnor_1 (xnor_1_out, x, y);
  and and_1 (and_1_out, or_1_out, not_1_out);
  not not_2 (not_2_out, not_3_out);
  and and_2 (and_2_out, nor_1_out, not_1_out);
  not not_3 (not_3_out, not_4_out);
  and and_3 (and_3_out, xor_1_out, _00___or___01___nor___10___xor___11___xnor[1]);
  not not_4 (not_4_out, _00___or___01___nor___10___xor___11___xnor[0]);
  and and_4 (and_4_out, xnor_1_out, _00___or___01___nor___10___xor___11___xnor[1]);
  and and_5 (and_5_out, and_1_out, not_2_out);
  and and_6 (and_6_out, and_2_out, not_3_out);
  or or_2 (s, and_5_out, and_6_out, and_7_out, and_8_out);
  and and_7 (and_7_out, and_3_out, not_4_out);
  and and_8 (and_8_out, and_4_out, _00___or___01___nor___10___xor___11___xnor[0]);
endmodule

module G0705 (
  input  x,
  input  y,
  input  [2:0] _0___nx___1___ny___2___AND___3___NAND___4___OR___5___NOR___6____XOR___7___XNOR,
  output s
);

  wire and_1_out, and_2_out, and_3_out, and_4_out, and_5_out, and_6_out, and_7_out, and_8_out, and_9_out,
       and_10_out, and_11_out, and_12_out, and_13_out, and_14_out, and_15_out, and_16_out, and_17_out,
       and_18_out, and_19_out, and_20_out, and_21_out, and_22_out, and_23_out, and_24_out, and_25_out,
       nand_1_out, nor_1_out, not_1_out, not_2_out, not_3_out, not_4_out, not_5_out, not_6_out, not_7_out,
       not_8_out, not_9_out, not_10_out, not_11_out, not_12_out, not_13_out, or_1_out, xnor_1_out, xor_1_out;

  not not_1 (not_1_out, x);
  not not_2 (not_2_out, y);
  and and_1 (and_1_out, x, y);
  nand nand_1 (nand_1_out, x, y);
  not not_3 (not_3_out, _0___nx___1___ny___2___AND___3___NAND___4___OR___5___NOR___6____XOR___7___XNOR[2]);
  or or_1 (or_1_out, x, y);
  nor nor_1 (nor_1_out, x, y);
  xor xor_1 (xor_1_out, x, y);
  xnor xnor_1 (xnor_1_out, x, y);
  and and_2 (and_2_out, not_1_out, not_3_out);
  and and_3 (and_3_out, not_2_out, not_3_out);
  not not_4 (not_4_out, not_5_out);
  and and_4 (and_4_out, and_1_out, not_3_out);
  and and_5 (and_5_out, nand_1_out, not_3_out);
  not not_5 (not_5_out, not_6_out);
  and and_6 (and_6_out, or_1_out, _0___nx___1___ny___2___AND___3___NAND___4___OR___5___NOR___6____XOR___7___XNOR[2]);
  and and_7 (and_7_out, nor_1_out, _0___nx___1___ny___2___AND___3___NAND___4___OR___5___NOR___6____XOR___7___XNOR[2]);
  not not_6 (not_6_out, _0___nx___1___ny___2___AND___3___NAND___4___OR___5___NOR___6____XOR___7___XNOR[1]);
  and and_8 (and_8_out, xor_1_out, _0___nx___1___ny___2___AND___3___NAND___4___OR___5___NOR___6____XOR___7___XNOR[2]);
  and and_9 (and_9_out, xnor_1_out, _0___nx___1___ny___2___AND___3___NAND___4___OR___5___NOR___6____XOR___7___XNOR[2]);
  and and_10 (and_10_out, and_2_out, not_4_out);
  and and_11 (and_11_out, and_10_out, not_7_out);
  not not_7 (not_7_out, not_8_out);
  and and_12 (and_12_out, and_3_out, not_4_out);
  and and_13 (and_13_out, and_12_out, not_8_out);
  not not_8 (not_8_out, not_9_out);
  and and_14 (and_14_out, and_4_out, not_5_out);
  and and_15 (and_15_out, and_14_out, not_9_out);
  not not_9 (not_9_out, not_10_out);
  and and_16 (and_16_out, and_5_out, not_5_out);
  and and_17 (and_17_out, and_16_out, not_10_out);
  not not_10 (not_10_out, not_11_out);
  and and_18 (and_18_out, and_6_out, not_6_out);
  and and_19 (and_19_out, and_18_out, not_11_out);
  not not_11 (not_11_out, not_12_out);
  and and_20 (and_20_out, and_7_out, not_6_out);
  and and_21 (and_21_out, and_20_out, not_12_out);
  not not_12 (not_12_out, not_13_out);
  and and_22 (and_22_out, and_8_out, _0___nx___1___ny___2___AND___3___NAND___4___OR___5___NOR___6____XOR___7___XNOR[1]);
  and and_23 (and_23_out, and_22_out, not_13_out);
  not not_13 (not_13_out, _0___nx___1___ny___2___AND___3___NAND___4___OR___5___NOR___6____XOR___7___XNOR[0]);
  and and_24 (and_24_out, and_9_out, _0___nx___1___ny___2___AND___3___NAND___4___OR___5___NOR___6____XOR___7___XNOR[1]);
  and and_25 (and_25_out, and_24_out, _0___nx___1___ny___2___AND___3___NAND___4___OR___5___NOR___6____XOR___7___XNOR[0]);
  or or_2 (s, and_11_out, and_13_out, and_15_out, and_17_out, and_19_out, and_21_out, and_23_out, and_25_out);
endmodule

module G0706a (
  input  [2:0] x,
  input  [2:0] y,
  input  _0___diferente___1___igual,
  output s
);

  wire and_1_out, and_2_out, and_3_out, and_4_out, and_5_out, and_6_out, and_7_out, not_1_out, or_1_out,
       xnor_1_out, xnor_2_out, xnor_3_out, xor_1_out, xor_2_out, xor_3_out;

  xor xor_1 (xor_1_out, x[2], y[2]);
  xor xor_2 (xor_2_out, x[1], y[1]);
  xor xor_3 (xor_3_out, x[0], y[0]);
  not not_1 (not_1_out, _0___diferente___1___igual);
  xnor xnor_1 (xnor_1_out, y[0], x[0]);
  xnor xnor_2 (xnor_2_out, y[1], x[1]);
  xnor xnor_3 (xnor_3_out, y[2], x[2]);
  and and_1 (and_1_out, xor_1_out, not_1_out);
  and and_2 (and_2_out, xor_2_out, not_1_out);
  and and_3 (and_3_out, xor_3_out, not_1_out);
  and and_4 (and_4_out, xnor_1_out, _0___diferente___1___igual);
  and and_5 (and_5_out, xnor_2_out, _0___diferente___1___igual);
  and and_6 (and_6_out, xnor_3_out, _0___diferente___1___igual);
  or or_1 (or_1_out, and_1_out, and_2_out, and_3_out);
  or or_2 (s, or_1_out, and_7_out);
  and and_7 (and_7_out, and_4_out, and_5_out, and_6_out);
endmodule

module G0706b (
  input  [2:0] x,
  input  _0___diferente___1___igual,
  input  [2:0] y,
  output s
);

  wire and_1_out, and_2_out, not_1_out, not_2_out, or_1_out, xor_1_out, xor_2_out, xor_3_out;

  xor xor_1 (xor_1_out, x[2], y[2]);
  or or_1 (or_1_out, xor_1_out, xor_2_out, xor_3_out);
  xor xor_2 (xor_2_out, x[1], y[1]);
  xor xor_3 (xor_3_out, x[0], y[0]);
  not not_1 (not_1_out, or_1_out);
  and and_1 (and_1_out, not_1_out, not_2_out);
  not not_2 (not_2_out, _0___diferente___1___igual);
  and and_2 (and_2_out, or_1_out, _0___diferente___1___igual);
  or or_2 (s, and_1_out, and_2_out);
endmodule
