// Logisim project G08.circ as structural Verilog: 7 circuits, main circuit Half adder
module Half_adder (
  input  A,
  input  B,
  output s0,
  output s1
);

  xor xor_1 (s0, B, A);
  and and_1 (s1, B, A);
endmodule

module Half_diff (
  input  A,
  input  B,
  output s0,
  output s1
);

  wire not_1_out;

  not not_1 (not_1_out, A);
  xor xor_1 (s0, B, A);
  and and_1 (s1, B, not_1_out);
endmodule

module G0801 (
  input  [3:0] A,
  input  [3:0] B,
  output [4:0] S
);

  wire half_adder_1_s1, half_adder_2_s0, half_adder_2_s1, half_adder_3_s0, half_adder_3_s1, half_adder_4_s0,
       half_adder_4_s1, half_adder_5_s1, half_adder_6_s1, half_adder_7_s0, half_adder_7_s1, half_adder_8_s0,
       half_adder_8_s1, half_adder_9_s0, half_adder_9_s1, half_adder_10_s0, half_adder_11_s1,
       half_adder_12_s0;

  Half_adder half_adder_1 (.s0(S[0]), .s1(half_adder_1_s1), .A(A[0]), .B(B[0]));
  Half_adder half_adder_2 (.s0(half_adder_2_s0), .s1(half_adder_2_s1), .A(A[1]), .B(B[1]));
  Half_adder half_adder_3 (.s0(half_adder_3_s0), .s1(half_adder_3_s1), .A(A[2]), .B(B[2]));
  Half_adder half_adder_4 (.s0(half_adder_4_s0), .s1(half_adder_4_s1), .A(A[3]), .B(B[3]));
  Half_adder half_adder_5 (.s0(S[1]), .s1(half_adder_5_s1), .A(half_adder_1_s1), .B(half_adder_2_s0));
  Half_adder half_adder_6 (.s0(S[2]), .s1(half_adder_6_s1), .A(half_adder_5_s1), .B(half_adder_7_s0));
  Half_adder half_adder_7 (.s0(half_adder_7_s0), .s1(half_adder_7_s1), .A(half_adder_2_s1), .B(half_adder_3_s0));
  Half_adder half_adder_8 (.s0(half_adder_8_s0), .s1(half_adder_8_s1), .A(half_adder_7_s1), .B(half_adder_9_s0));
  Half_adder half_adder_9 (.s0(half_adder_9_s0), .s1(half_adder_9_s1), .A(half_adder_3_s1), .B(half_adder_4_s0));
  Half_adder half_adder_10 (.s0(half_adder_10_s0), .A(half_adder_9_s1), .B(half_adder_4_s1));  // open: s1
  Half_adder half_adder_11 (.s0(S[3]), .s1(half_adder_11_s1), .A(half_adder_6_s1), .B(half_adder_8_s0));
  Half_adder half_adder_12 (.s0(half_adder_12_s0), .A(half_adder_8_s1), .B(half_adder_10_s0));  // open: s1
  Half_adder half_adder_13 (.s0(S[4]), .A(half_adder_11_s1), .B(half_adder_12_s0));  // open: s1
endmodule

module G0802 (
  input  in_1,
  input  in_2,
  input  in_3,
  output out_4,
  output out_5
);

  wire half_diff_1_s0, half_diff_1_s1, half_diff_2_s1;

  Half_diff half_diff_1 (.s0(half_diff_1_s0), .s1(half_diff_1_s1), .A(in_3), .B(in_2));
  Half_diff half_diff_2 (.s0(out_4), .s1(half_diff_2_s1), .A(half_diff_1_s0), .B(in_1));
  or or_1 (out_5, half_diff_2_s1, half_diff_1_s1);
endmodule

module G0803 (
  input  [3:0] A,
  input  [3:0] B,
  output S
);

  wire xnor_1_out, xnor_2_out, xnor_3_out, xnor_4_out;

  xnor xnor_1 (xnor_1_out, A[0], B[0]);
  xnor xnor_2 (xnor_2_out, A[1], B[1]);
  xnor xnor_3 (xnor_3_out, A[2], B[2]);
  xnor xnor_4 (xnor_4_out, A[3], B[3]);
  and and_1 (S, xnor_1_out, xnor_2_out, xnor_3_out, xnor_4_out);
endmodule

module G0804 (
  input  [3:0] A,
  input  [3:0] B,
  output S
);

  wire xor_1_out, xor_2_out, xor_3_out, xor_4_out;

  xor xor_1 (xor_1_out, A[0], B[0]);
  xor xor_2 (xor_2_out, A[1], B[1]);
  xor xor_3 (xor_3_out, A[2], B[2]);
  xor xor_4 (xor_4_out, A[3], B[3]);
  or or_1 (S, xor_1_out, xor_2_out, xor_3_out, xor_4_out);
endmodule

module G0805 (
  input  [5:0] A,
  output [6:0] B
);

  wire half_adder_1_s1, half_adder_2_s1, half_adder_3_s1, half_adder_4_s1, half_adder_5_s1, not_1_out,
       not_2_out, not_3_out, not_4_out, not_5_out, not_6_out, not_7_out, plus_1_out;

  not not_1 (not_1_out, A[0]);
  not not_2 (not_2_out, A[0]);
  not not_3 (not_3_out, A[1]);
  not not_4 (not_4_out, A[2]);
  not not_5 (not_5_out, A[3]);
  not not_6 (not_6_out, A[4]);
  not not_7 (not_7_out, A[5]);
  or plus_1 (plus_1_out, not_1_out, A[0]);
  Half_adder half_adder_1 (.s0(B[0]), .s1(half_adder_1_s1), .A(plus_1_out), .B(not_2_out));
  Half_adder half_adder_2 (.s0(B[1]), .s1(half_adder_2_s1), .A(half_adder_1_s1), .B(not_3_out));
  Half_adder half_adder_3 (.s0(B[2]), .s1(half_adder_3_s1), .A(half_adder_2_s1), .B(not_4_out));
  Half_adder half_adder_4 (.s0(B[3]), .s1(half_adder_4_s1), .A(half_adder_3_s1), .B(not_5_out));
  Half_adder half_adder_5 (.s0(B[4]), .s1(half_adder_5_s1), .A(half_adder_4_s1), .B(not_6_out));
  Half_adder half_adder_6 (.s0(B[5]), .s1(B[6]), .A(half_adder_5_s1), .B(not_7_out));
endmodule
