// Logisim project G11.circ as structural Verilog: 4 circuits, main circuit G1101
module Stack (
  input  in_1,
  input  in_2,
  input  in_3,
  output out_4,
  output out_5,
  output out_6,
  output out_7
);

  D_Flip_Flop #(.Pre_Clr_Positions("LEGACY"), .NewFFLayout("false")) d_ff_1 (
    .clk(in_1), .D(in_2), .Q(out_4), .reset(in_3));  // open: Qn, preset
  D_Flip_Flop #(.Pre_Clr_Positions("LEGACY"), .NewFFLayout("false")) d_ff_2 (
    .clk(in_1), .D(out_4), .Q(out_5), .reset(in_3));  // open: Qn, preset
  D_Flip_Flop #(.Pre_Clr_Positions("LEGACY"), .NewFFLayout("false")) d_ff_3 (
    .clk(in_1), .D(out_5), .Q(out_6), .reset(in_3));  // open: Qn, preset
  D_Flip_Flop #(.Pre_Clr_Positions("LEGACY"), .NewFFLayout("false")) d_ff_4 (
    .clk(in_1), .D(out_6), .Q(out_7), .reset(in_3));  // open: Qn, preset
endmodule

module G1101 (
  input  clk,
  input  in,
  input  clr,
  output out
);

  wire not_1_out, or_1_out, stack_1_out_4, stack_1_out_5, stack_1_out_6, stack_1_out_7;

  and and_1 (out, stack_1_out_7, stack_1_out_6, not_1_out, stack_1_out_4);
  or or_1 (or_1_out, out, clk);
  Stack stack_1 (
    .in_2(in), .out_4(stack_1_out_4), .out_5(stack_1_out_5), .out_6(stack_1_out_6), .out_7(stack_1_out_7),
    .in_1(or_1_out), .in_3(clr));
  not not_1 (not_1_out, stack_1_out_5);

  // Notes on the sheet:
  //   1101
endmodule

module G1101b (
  input  x,
  input  clk,
  input  clr,
  output d1_d2_prime_x
);

  wire and_1_out, and_2_out, d_ff_1_q, d_ff_2_q, d_ff_2_qn, or_1_out;

  and and_1 (and_1_out, d_ff_1_q, d_ff_2_q);
  and and_2 (and_2_out, x, d_ff_2_q);
  or or_1 (or_1_out, and_1_out, and_2_out);
  // Probe on d_ff_1_q
  // Probe on d_ff_2_q
  D_Flip_Flop #(.Pre_Clr_Positions("LEGACY"), .NewFFLayout("false")) d_ff_1 (
    .clk(clk), .D(or_1_out), .Q(d_ff_1_q), .reset(clr));  // open: Qn, preset
  D_Flip_Flop #(.Pre_Clr_Positions("LEGACY"), .NewFFLayout("false")) d_ff_2 (
    .clk(clk), .D(x), .Q(d_ff_2_q), .Qn(d_ff_2_qn), .reset(clr));  // open: preset
  and and_3 (d1_d2_prime_x, x, d_ff_1_q, d_ff_2_qn);

  // Notes on the sheet:
  //   d1.d2
  //   d2.x
  //   d1
  //   d2
endmodule

module G1102 (
  input  clk,
  input  in,
  input  clr,
  output out
);

  wire and_1_out, not_1_out, or_1_out, stack_1_out_4, stack_1_out_5, stack_1_out_6, stack_1_out_7;

  or or_1 (or_1_out, and_1_out, clk);
  and and_1 (and_1_out, stack_1_out_4, not_1_out, stack_1_out_6, stack_1_out_7);
  not not_1 (not_1_out, stack_1_out_5);
  Stack stack_1 (
    .in_2(in), .out_4(stack_1_out_4), .out_5(stack_1_out_5), .out_6(stack_1_out_6), .out_7(stack_1_out_7),
    .in_1(or_1_out), .in_3(clr));
  D_Flip_Flop #(.Pre_Clr_Positions("LEGACY"), .NewFFLayout("false")) d_ff_1 (
    .clk(clk), .D(and_1_out), .Q(out), .reset(clr));  // open: Qn, preset

  // Notes on the sheet:
  //   1101
endmodule
