// Logisim project PA01e.circ as structural Verilog: 1 circuit, main circuit main
module main (
  input  A,
  input  B,
  input  C,
  input  D,
  output out_5
);

  wire nand_1_out, nand_2_out, nand_3_out, not_1_out, not_2_out, not_3_out, not_4_out, not_5_out, not_6_out,
       not_7_out, not_8_out, xor_1_out;

  not not_1 (not_1_out, D);
  not not_2 (not_2_out, C);
  not not_3 (not_3_out, D);
  not not_4 (not_4_out, A);
  not not_5 (not_5_out, B);
  xor xor_1 (xor_1_out, B, not_1_out);
  nand nand_1 (nand_1_out, B, not_2_out, not_3_out);
  nand nand_2 (nand_2_out, not_4_out, C, xor_1_out);
  nand nand_3 (nand_3_out, A, not_5_out, C, D);
  not not_6 (not_6_out, nand_1_out);
  or or_1 (out_5, not_6_out, not_7_out, not_8_out);
  not not_7 (not_7_out, nand_2_out);
  not not_8 (not_8_out, nand_3_out);

  // Notes on the sheet:
  //   Simplificar   ^
endmodule
