// Logisim project PA1.circ as structural Verilog: 3 circuits, main circuit PA01e
module PA01e (
  input  A,
  input  B,
  input  C,
  input  D,
  output out_5
);

  wire nand_1_out, nand_2_out, nand_3_out, not_1_out, not_2_out, not_3_out, not_4_out, not_5_out, not_6_out,
       not_7_out, not_8_out, xor_1_out;

  not not_1 (not_1_out, D);
  not not_2 (not_2_out, C);
  not not_3 (not_3_out, D);
  not not_4 (not_4_out, A);
  not not_5 (not_5_out, B);
  xor xor_1 (xor_1_out, B, not_1_out);
  nand nand_1 (nand_1_out, B, not_2_out, not_3_out);
  nand nand_2 (nand_2_out, not_4_out, C, xor_1_out);
  nand nand_3 (nand_3_out, A, not_5_out, C, D);
  not not_6 (not_6_out, nand_1_out);
  or or_1 (out_5, not_6_out, not_7_out, not_8_out);
  not not_7 (not_7_out, nand_2_out);
  not not_8 (not_8_out, nand_3_out);

  // Notes on the sheet:
  //   Simplificar   ^
endmodule

module PA01f (
  input  A,
  input  B,
  input  C,
  input  D,
  output out_5
);

  wire buffer_1_out, nor_1_out, nor_2_out, nor_3_out, nor_4_out, nor_5_out, nor_6_out, not_1_out, not_2_out,
       not_3_out, not_4_out, not_5_out, not_6_out, not_7_out, not_8_out, not_9_out, not_10_out, not_11_out,
       not_12_out, not_13_out, not_14_out, not_15_out;

  buf buffer_1 (buffer_1_out, A);
  nor nor_1 (nor_1_out, B, C, D);
  nor nor_2 (nor_2_out, C, not_1_out);
  not not_1 (not_1_out, D);
  nor nor_3 (nor_3_out, A, not_2_out, B);
  not not_2 (not_2_out, D);
  not not_3 (not_3_out, A);
  not not_4 (not_4_out, B);
  nor nor_4 (nor_4_out, not_3_out, not_4_out, not_5_out);
  not not_5 (not_5_out, C);
  not not_6 (not_6_out, B);
  nor nor_5 (nor_5_out, not_6_out, not_7_out, B);
  not not_7 (not_7_out, C);
  not not_8 (not_8_out, buffer_1_out);
  not not_9 (not_9_out, C);
  nor nor_6 (nor_6_out, not_8_out, not_9_out, B);
  not not_10 (not_10_out, nor_1_out);
  not not_11 (not_11_out, nor_2_out);
  not not_12 (not_12_out, nor_3_out);
  not not_13 (not_13_out, nor_4_out);
  not not_14 (not_14_out, nor_5_out);
  not not_15 (not_15_out, nor_6_out);
  and and_1 (out_5, not_10_out, not_11_out, not_12_out, not_13_out, not_14_out, not_15_out);
endmodule

module PA02 (
  input  x,
  input  y,
  output out_3
);

  wire not_1_out, not_2_out, not_3_out, or_1_out, or_2_out;

  or or_1 (or_1_out, y, not_1_out);
  not not_1 (not_1_out, x);
  not not_2 (not_2_out, y);
  or or_2 (or_2_out, not_2_out, x);
  and and_1 (out_3, or_1_out, not_3_out);
  not not_3 (not_3_out, or_2_out);
endmodule
