// Logisim project Decoder.circ as structural Verilog: 4 circuits, main circuit Decoder
module Decoder (
  input  in_1,
  input  in_2,
  input  in_3,
  input  in_4,
  output out_5,
  output out_6,
  output out_7,
  output out_8
);

  wire not_1_out, not_2_out, not_3_out, not_4_out;

  not not_1 (not_1_out, in_1);
  not not_2 (not_2_out, in_4);
  not not_3 (not_3_out, in_2);
  not not_4 (not_4_out, in_3);
  and Load (out_5, in_4, not_4_out, not_3_out, not_1_out);
  and add (out_6, not_2_out, in_3, not_3_out, not_1_out);
  and sub (out_7, not_2_out, not_4_out, in_2, not_1_out);
  and add_2 (out_8, not_2_out, not_4_out, not_3_out, in_1);
endmodule

module dd (
  input  [3:0] in_1,
  output out_2,
  output out_3,
  output out_4,
  output out_5
);

  Decoder decoder_1 (
    .out_5(out_5), .out_6(out_4), .out_7(out_3), .out_8(out_2), .in_1(in_1[3]), .in_2(in_1[2]),
    .in_3(in_1[1]), .in_4(in_1[0]));
endmodule

module Ring (
  input  Clk,
  input  Load,
  output out_3,
  output out_4,
  output out_5,
  output out_6
);

  D_Flip_Flop #(.Pre_Clr_Positions("LEGACY"), .NewFFLayout("false")) d_ff_1 (
    .clk(Clk), .D(out_6), .Q(out_3), .preset(Load));  // open: Qn, reset
  D_Flip_Flop #(.Pre_Clr_Positions("LEGACY"), .NewFFLayout("false")) d_ff_2 (
    .clk(Clk), .D(out_3), .Q(out_4), .reset(Load));  // open: Qn, preset
  D_Flip_Flop #(.Pre_Clr_Positions("LEGACY"), .NewFFLayout("false")) d_ff_3 (
    .clk(Clk), .D(out_4), .Q(out_5), .reset(Load));  // open: Qn, preset
  D_Flip_Flop #(.Pre_Clr_Positions("LEGACY"), .NewFFLayout("false")) d_ff_4 (
    .clk(Clk), .D(out_5), .Q(out_6), .reset(Load));  // open: Qn, preset
endmodule

module asd (
  input  [3:0] in_1,
  input  in_2
);

  wire clock_1_out, d_ff_1_q, d_ff_1_qn, dd_1_out_2, dd_1_out_3, dd_1_out_4, dd_1_out_5, or_1_out,
       ring_1_out_3, ring_1_out_4, ring_1_out_5, ring_1_out_6;

  dd dd_1 (.in_1(in_1), .out_2(dd_1_out_2), .out_3(dd_1_out_3), .out_4(dd_1_out_4), .out_5(dd_1_out_5));
  Clock clock_1 (.out(clock_1_out));
  or or_1 (or_1_out, clock_1_out, d_ff_1_qn);
  Ring ring_1 (
    .Clk(clock_1_out), .Load(d_ff_1_q), .out_3(ring_1_out_3), .out_4(ring_1_out_4), .out_5(ring_1_out_5),
    .out_6(ring_1_out_6));
  D_Flip_Flop #(.Pre_Clr_Positions("LEGACY"), .NewFFLayout("false")) d_ff_1 (
    .clk(or_1_out), .Q(d_ff_1_q), .Qn(d_ff_1_qn), .reset(in_2));  // open: D, preset
  // AND_Gate and_1 has open pins: in0=ring_1_out_3, in1=dd_1_out_5, out=open
  // AND_Gate and_2 has open pins: in0=ring_1_out_5, in1=dd_1_out_3, out=open
  // AND_Gate and_3 has open pins: in0=ring_1_out_4, in1=dd_1_out_4, out=open
  // AND_Gate and_4 has open pins: in0=ring_1_out_6, in1=dd_1_out_2, out=open
endmodule
