// Logisim project Flip-Flop arrays.circ as structural Verilog
module Left_Right (
  input  in_1,
  input  in_2
);

  wire clock_1_out, d_ff_1_q, d_ff_2_q, d_ff_3_q;

  Clock clock_1 (.out(clock_1_out));
  D_Flip_Flop #(.Pre_Clr_Positions("LEGACY"), .NewFFLayout("false")) d_ff_1 (
    .clk(clock_1_out), .D(d_ff_2_q), .Q(d_ff_1_q), .reset(in_2));  // open: Qn, preset
  D_Flip_Flop #(.Pre_Clr_Positions("LEGACY"), .NewFFLayout("false")) d_ff_2 (
    .clk(clock_1_out), .D(in_1), .Q(d_ff_2_q), .reset(in_2));  // open: Qn, preset
  D_Flip_Flop #(.Pre_Clr_Positions("LEGACY"), .NewFFLayout("false")) d_ff_3 (
    .clk(clock_1_out), .D(d_ff_1_q), .Q(d_ff_3_q), .reset(in_2));  // open: Qn, preset
  D_Flip_Flop #(.Pre_Clr_Positions("LEGACY"), .NewFFLayout("false")) d_ff_4 (
    .clk(clock_1_out), .D(d_ff_3_q), .reset(in_2));  // open: Q, Qn, preset
endmodule

module Right_Left (
  input  in_1,
  input  in_2
);

  wire clock_1_out, d_ff_2_q, d_ff_3_q, d_ff_4_q;

  Clock clock_1 (.out(clock_1_out));
  D_Flip_Flop #(.Pre_Clr_Positions("LEGACY"), .NewFFLayout("false")) d_ff_1 (
    .clk(clock_1_out), .D(d_ff_2_q), .reset(in_2));  // open: Q, Qn, preset
  D_Flip_Flop #(.Pre_Clr_Positions("LEGACY"), .NewFFLayout("false")) d_ff_2 (
    .clk(clock_1_out), .D(d_ff_3_q), .Q(d_ff_2_q), .reset(in_2));  // open: Qn, preset
  D_Flip_Flop #(.Pre_Clr_Positions("LEGACY"), .NewFFLayout("false")) d_ff_3 (
    .clk(clock_1_out), .D(d_ff_4_q), .Q(d_ff_3_q), .reset(in_2));  // open: Qn, preset
  D_Flip_Flop #(.Pre_Clr_Positions("LEGACY"), .NewFFLayout("false")) d_ff_4 (
    .clk(clock_1_out), .D(in_1), .Q(d_ff_4_q), .reset(in_2));  // open: Qn, preset
endmodule

module Load (
  input  X,
  input  Clr,
  input  Load,
  input  in_4,
  input  in_5,
  input  in_6,
  input  in_7,
  output out_8
);

  wire and_1_out, and_2_out, and_3_out, and_4_out, Clk_out, d_ff_1_q, d_ff_2_q, d_ff_3_q;

  Clock Clk (.out(Clk_out));
  D_Flip_Flop #(.Pre_Clr_Positions("LEGACY"), .NewFFLayout("false")) d_ff_1 (
    .clk(Clk_out), .D(X), .Q(d_ff_1_q), .preset(and_1_out), .reset(Clr));  // open: Qn
  and and_1 (and_1_out, Load, in_4);
  D_Flip_Flop #(.Pre_Clr_Positions("LEGACY"), .NewFFLayout("false")) d_ff_2 (
    .clk(Clk_out), .D(d_ff_1_q), .Q(d_ff_2_q), .preset(and_2_out), .reset(Clr));  // open: Qn
  and and_2 (and_2_out, Load, in_5);
  D_Flip_Flop #(.Pre_Clr_Positions("LEGACY"), .NewFFLayout("false")) d_ff_3 (
    .clk(Clk_out), .D(d_ff_2_q), .Q(d_ff_3_q), .preset(and_3_out), .reset(Clr));  // open: Qn
  and and_3 (and_3_out, Load, in_6);
  D_Flip_Flop #(.Pre_Clr_Positions("LEGACY"), .NewFFLayout("false")) d_ff_4 (
    .clk(Clk_out), .D(d_ff_3_q), .Q(out_8), .preset(and_4_out), .reset(Clr));  // open: Qn
  and and_4 (and_4_out, Load, in_7);

  // Notes on the sheet:
  //   Arma?
endmodule

module Ring (
  input  in_1
);

  wire clock_1_out, d_ff_1_q, d_ff_2_q, d_ff_3_q, d_ff_4_q;

  Clock clock_1 (.out(clock_1_out));
  D_Flip_Flop #(.Pre_Clr_Positions("LEGACY"), .NewFFLayout("false")) d_ff_1 (
    .clk(clock_1_out), .D(d_ff_4_q), .Q(d_ff_1_q), .preset(in_1));  // open: Qn, reset
  // Probe on d_ff_1_q
  // Probe on d_ff_2_q
  D_Flip_Flop #(.Pre_Clr_Positions("LEGACY"), .NewFFLayout("false")) d_ff_2 (
    .clk(clock_1_out), .D(d_ff_1_q), .Q(d_ff_2_q), .reset(in_1));  // open: Qn, preset
  // Probe on d_ff_3_q
  D_Flip_Flop #(.Pre_Clr_Positions("LEGACY"), .NewFFLayout("false")) d_ff_3 (
    .clk(clock_1_out), .D(d_ff_2_q), .Q(d_ff_3_q), .reset(in_1));  // open: Qn, preset
  // Probe on d_ff_4_q
  D_Flip_Flop #(.Pre_Clr_Positions("LEGACY"), .NewFFLayout("false")) d_ff_4 (
    .clk(clock_1_out), .D(d_ff_3_q), .Q(d_ff_4_q), .reset(in_1));  // open: Qn, preset
endmodule

module Twisted_Ring (
  input  in_1
);

  wire clock_1_out, d_ff_1_q, d_ff_2_q, d_ff_3_q, d_ff_4_qn, not_1_out;

  Clock clock_1 (.out(clock_1_out));
  D_Flip_Flop #(.Pre_Clr_Positions("LEGACY"), .NewFFLayout("false")) d_ff_1 (
    .clk(clock_1_out), .D(d_ff_4_qn), .Q(d_ff_1_q), .preset(in_1));  // open: Qn, reset
  // Probe on d_ff_1_q
  // Probe on d_ff_2_q
  D_Flip_Flop #(.Pre_Clr_Positions("LEGACY"), .NewFFLayout("false")) d_ff_2 (
    .clk(clock_1_out), .D(d_ff_1_q), .Q(d_ff_2_q), .reset(in_1));  // open: Qn, preset
  // Probe on d_ff_3_q
  D_Flip_Flop #(.Pre_Clr_Positions("LEGACY"), .NewFFLayout("false")) d_ff_3 (
    .clk(clock_1_out), .D(d_ff_2_q), .Q(d_ff_3_q), .reset(in_1));  // open: Qn, preset
  not not_1 (not_1_out, d_ff_4_qn);
  // Probe on not_1_out
  D_Flip_Flop #(.Pre_Clr_Positions("LEGACY"), .NewFFLayout("false")) d_ff_4 (
    .clk(clock_1_out), .D(d_ff_3_q), .Qn(d_ff_4_qn), .reset(in_1));  // open: Q, preset
endmodule

module Release (
  input  X,
  input  Clr,
  input  Rls,
  output out_4,
  output out_5,
  output out_6,
  output out_7
);

  wire Clk_out, d_ff_1_q, d_ff_2_q, d_ff_3_q, d_ff_4_q;

  Clock Clk (.out(Clk_out));
  and and_1 (out_4, Rls, d_ff_1_q);
  D_Flip_Flop #(.Pre_Clr_Positions("LEGACY"), .NewFFLayout("false")) d_ff_1 (
    .clk(Clk_out), .D(X), .Q(d_ff_1_q), .reset(Clr));  // open: Qn, preset
  and and_2 (out_5, Rls, d_ff_3_q);
  D_Flip_Flop #(.Pre_Clr_Positions("LEGACY"), .NewFFLayout("false")) d_ff_2 (
    .clk(Clk_out), .D(d_ff_3_q), .Q(d_ff_2_q), .reset(Clr));  // open: Qn, preset
  D_Flip_Flop #(.Pre_Clr_Positions("LEGACY"), .NewFFLayout("false")) d_ff_3 (
    .clk(Clk_out), .D(d_ff_1_q), .Q(d_ff_3_q), .reset(Clr));  // open: Qn, preset
  and and_3 (out_6, Rls, d_ff_2_q);
  D_Flip_Flop #(.Pre_Clr_Positions("LEGACY"), .NewFFLayout("false")) d_ff_4 (
    .clk(Clk_out), .D(d_ff_2_q), .Q(d_ff_4_q), .reset(Clr));  // open: Qn, preset
  and and_4 (out_7, Rls, d_ff_4_q);

  // Notes on the sheet:
  //   Arma?
endmodule

module Async_Sum (
  input  in_1,
  input  in_2
);

  wire button_1_out, clock_1_out, j_k_ff_1_q, j_k_ff_1_qn, j_k_ff_2_q, j_k_ff_2_qn, j_k_ff_3_q, j_k_ff_3_qn,
       j_k_ff_4_q, or_1_out;

  Clock clock_1 (.out(clock_1_out));
  Button button_1 (.out(button_1_out));
  or or_1 (or_1_out, clock_1_out, button_1_out);
  // Probe on j_k_ff_4_q
  J_K_Flip_Flop #(.Pre_Clr_Positions("LEGACY"), .NewFFLayout("false")) j_k_ff_1 (
    .J(in_1), .clk(or_1_out), .K(in_1), .Q(j_k_ff_1_q), .Qn(j_k_ff_1_qn), .reset(in_2));  // open: preset
  // Probe on j_k_ff_3_q
  J_K_Flip_Flop #(.Pre_Clr_Positions("LEGACY"), .NewFFLayout("false")) j_k_ff_2 (
    .J(in_1), .clk(j_k_ff_1_qn), .K(in_1), .Q(j_k_ff_2_q), .Qn(j_k_ff_2_qn), .reset(in_2));  // open: preset
  J_K_Flip_Flop #(.Pre_Clr_Positions("LEGACY"), .NewFFLayout("false")) j_k_ff_3 (
    .J(in_1), .clk(j_k_ff_2_qn), .K(in_1), .Q(j_k_ff_3_q), .Qn(j_k_ff_3_qn), .reset(in_2));  // open: preset
  // Probe on j_k_ff_2_q
  // Probe on j_k_ff_1_q
  J_K_Flip_Flop #(.Pre_Clr_Positions("LEGACY"), .NewFFLayout("false")) j_k_ff_4 (
    .J(in_1), .clk(j_k_ff_3_qn), .K(in_1), .Q(j_k_ff_4_q), .reset(in_2));  // open: Qn, preset
endmodule

module For (
  input  Clk,
  input  X,
  input  Clr,
  input  Load,
  input  in_5,
  input  in_6,
  input  in_7,
  input  in_8
);

  wire and_1_out, and_2_out, and_3_out, and_4_out, and_5_out, button_1_out, j_k_ff_1_qn, j_k_ff_2_q,
       j_k_ff_2_qn, j_k_ff_3_qn, j_k_ff_4_q, or_1_out, or_2_out;

  or or_1 (or_1_out, Clk, button_1_out);
  or or_2 (or_2_out, Clr, and_1_out);
  and and_1 (and_1_out, j_k_ff_1_qn, j_k_ff_2_q, j_k_ff_3_qn, j_k_ff_4_q);
  Button button_1 (.out(button_1_out));
  J_K_Flip_Flop #(.Pre_Clr_Positions("LEGACY"), .NewFFLayout("false")) j_k_ff_1 (
    .J(X), .clk(or_1_out), .K(X), .Qn(j_k_ff_1_qn), .preset(and_2_out), .reset(or_2_out));  // open: Q
  and and_2 (and_2_out, Load, in_5);
  J_K_Flip_Flop #(.Pre_Clr_Positions("LEGACY"), .NewFFLayout("false")) j_k_ff_2 (
    .J(X), .clk(j_k_ff_1_qn), .K(X), .Q(j_k_ff_2_q), .Qn(j_k_ff_2_qn), .preset(and_3_out), .reset(or_2_out));
  and and_3 (and_3_out, Load, in_6);
  J_K_Flip_Flop #(.Pre_Clr_Positions("LEGACY"), .NewFFLayout("false")) j_k_ff_3 (
    .J(X), .clk(j_k_ff_2_qn), .K(X), .Qn(j_k_ff_3_qn), .preset(and_4_out), .reset(or_2_out));  // open: Q
  and and_4 (and_4_out, Load, in_7);
  J_K_Flip_Flop #(.Pre_Clr_Positions("LEGACY"), .NewFFLayout("false")) j_k_ff_4 (
    .J(X), .clk(j_k_ff_3_qn), .K(X), .Q(j_k_ff_4_q), .preset(and_5_out), .reset(or_2_out));  // open: Qn
  and and_5 (and_5_out, Load, in_8);

  // Notes on the sheet:
  //   For (10)
endmodule

module Freq_Div (
  input  in_1,
  input  in_2,
  input  in_3,
  output out_4,
  output out_5
);

  wire A_q, B_qn, clock_1_out, digital_oscilloscope_1_p4, digital_oscilloscope_1_p7,
       digital_oscilloscope_1_p10, nand_1_out, nand_3_out;

  Clock clock_1 (.out(clock_1_out));
  nand nand_1 (nand_1_out, digital_oscilloscope_1_p4, A_q);
  D_Flip_Flop #(.Pre_Clr_Positions("LEGACY"), .NewFFLayout("false")) A (
    .clk(clock_1_out), .D(nand_1_out), .Q(A_q), .reset(in_1));  // open: Qn, preset
  // Digital_Oscilloscope digital_oscilloscope_1: pin names not known; wires that end beside it: nand_1_out, clock_1_out, A_q, digital_oscilloscope_1_p4, out_4, out_5, digital_oscilloscope_1_p7, digital_oscilloscope_1_p7, in_2, digital_oscilloscope_1_p10, in_3, digital_oscilloscope_1_p10
  D_Flip_Flop #(.Pre_Clr_Positions("LEGACY"), .NewFFLayout("false")) B (
    .clk(clock_1_out), .D(A_q), .Q(digital_oscilloscope_1_p4), .Qn(B_qn), .reset(in_1));  // open: preset
  nand nand_2 (out_4, clock_1_out, A_q, B_qn);
  nand nand_3 (nand_3_out, clock_1_out, B_qn);
  nand nand_4 (out_5, A_q, nand_3_out);
endmodule

module Freq_Div_2 (
  input  in_1,
  input  in_2,
  output out_3,
  output out_4
);

  wire A_2_q, A_q, A_qn, B_qn, clock_1_out, digital_oscilloscope_1_p4, digital_oscilloscope_1_p7,
       digital_oscilloscope_1_p9, digital_oscilloscope_1_p12, digital_oscilloscope_1_p13, nand_1_out,
       nand_2_out, nand_3_out;

  Clock clock_1 (.out(clock_1_out));
  nand nand_1 (nand_1_out, digital_oscilloscope_1_p4, A_q);
  D_Flip_Flop #(.Pre_Clr_Positions("LEGACY"), .NewFFLayout("false")) A (
    .clk(clock_1_out), .D(nand_1_out), .Q(A_q), .Qn(A_qn));  // open: preset, reset
  // Digital_Oscilloscope digital_oscilloscope_1: pin names not known; wires that end beside it: nand_1_out, clock_1_out, A_q, digital_oscilloscope_1_p4, out_3, out_4, digital_oscilloscope_1_p7, in_1, digital_oscilloscope_1_p9, digital_oscilloscope_1_p7, digital_oscilloscope_1_p9, digital_oscilloscope_1_p12, digital_oscilloscope_1_p13, digital_oscilloscope_1_p12, in_2, digital_oscilloscope_1_p13
  D_Flip_Flop #(.Pre_Clr_Positions("LEGACY"), .NewFFLayout("false")) B (
    .clk(clock_1_out), .D(A_q), .Q(digital_oscilloscope_1_p4), .Qn(B_qn));  // open: preset, reset
  nand nand_2 (nand_2_out, clock_1_out, B_qn);
  nand nand_3 (nand_3_out, B_qn, A_qn);
  nand nand_4 (out_3, A_q, nand_2_out);
  D_Flip_Flop #(.Pre_Clr_Positions("LEGACY"), .NewFFLayout("false")) A_2 (
    .clk(nand_2_out), .D(nand_3_out), .Q(A_2_q));  // open: Qn, preset, reset
  nand nand_5 (out_4, A_q, A_2_q);
endmodule

module fq3 (
  input  in_1,
  input  in_2,
  output out_3,
  output out_4
);

  wire A_2_q, A_q, clock_1_out, digital_oscilloscope_1_p4, digital_oscilloscope_1_p7,
       digital_oscilloscope_1_p9, digital_oscilloscope_1_p12, digital_oscilloscope_1_p13, nand_1_out;

  Clock clock_1 (.out(clock_1_out));
  nand nand_1 (nand_1_out, digital_oscilloscope_1_p4, A_q);
  D_Flip_Flop #(.Pre_Clr_Positions("LEGACY"), .NewFFLayout("false")) A (
    .clk(clock_1_out), .D(nand_1_out), .Q(A_q));  // open: Qn, preset, reset
  // Digital_Oscilloscope digital_oscilloscope_1: pin names not known; wires that end beside it: nand_1_out, clock_1_out, A_q, digital_oscilloscope_1_p4, out_3, out_4, digital_oscilloscope_1_p7, in_1, digital_oscilloscope_1_p9, digital_oscilloscope_1_p7, digital_oscilloscope_1_p9, digital_oscilloscope_1_p12, digital_oscilloscope_1_p13, digital_oscilloscope_1_p12, in_2, digital_oscilloscope_1_p13
  D_Flip_Flop #(.Pre_Clr_Positions("LEGACY"), .NewFFLayout("false")) B (
    .clk(clock_1_out), .D(A_q), .Q(digital_oscilloscope_1_p4));  // open: Qn, preset, reset
  D_Flip_Flop #(.Pre_Clr_Positions("LEGACY"), .NewFFLayout("false")) A_2 (
    .clk(clock_1_out), .D(digital_oscilloscope_1_p4), .Q(A_2_q));  // open: Qn, preset, reset
  nand nand_2 (out_3, A_q, A_2_q);
  nand nand_3 (out_4, A_q, digital_oscilloscope_1_p4);
endmodule
