// Logisim project Flip.circ as structural Verilog: 4 circuits, main circuit main
module Flip_Flop (
  input  in_1,
  input  in_2,
  input  in_3,
  input  in_4,
  output out_5,
  output out_6
);

  wire not_1_out, not_2_out, or_1_out, or_2_out;

  or or_1 (or_1_out, in_1, in_2);
  not not_1 (not_1_out, or_1_out);
  not not_2 (not_2_out, or_2_out);
  or or_2 (or_2_out, in_3, in_4);
  nand nand_1 (out_6, not_1_out, out_5);
  nand nand_2 (out_5, out_6, not_2_out);
endmodule

module Catch (
  input  in_1,
  input  in_2,
  output out_3
);

  wire and_1_out, and_2_out;

  and and_1 (and_1_out, in_1, in_2);
  and and_2 (and_2_out, in_2, out_3);
  or or_1 (out_3, and_1_out, and_2_out);
endmodule

module C_Flip_Flop (
  input  x,
  input  Clk,
  input  _1,
  input  _0,
  output s,
  output s_prime
);

  wire catch_1_out_3, demultiplexer_1_out0, demultiplexer_1_out1;

  Catch catch_1 (.in_1(x), .in_2(Clk), .out_3(catch_1_out_3));
  Demultiplexer #(.enable("false")) demultiplexer_1 (
    .out0(demultiplexer_1_out0), .out1(demultiplexer_1_out1), .in(Clk), .sel(catch_1_out_3));
  Flip_Flop ff_1 (
    .out_5(s), .out_6(s_prime), .in_1(demultiplexer_1_out0), .in_2(_0), .in_3(demultiplexer_1_out1), .in_4(_1));
endmodule

module main (
  input  in_1,
  input  in_2,
  output out_3,
  output out_4
);

  D_Flip_Flop #(.Pre_Clr_Positions("LEGACY"), .NewFFLayout("false")) d_ff_1 (
    .clk(in_1), .D(in_2));  // open: Q, Qn, preset, reset
  C_Flip_Flop c_ff_1 (.Clk(in_2), .x(in_1), .s(out_3), .s_prime(out_4));  // open: _1, _0
endmodule
