// Logisim project RAM.circ as structural Verilog: 7 circuits, main circuit Flip-Flop
module Flip_Flop (
  input  in_1,
  input  in_2,
  input  in_3,
  input  in_4,
  input  in_5,
  input  in_6,
  output out_7,
  output out_8,
  output out_9,
  output out_10,
  output out_11,
  output out_12,
  output out_13,
  output out_14
);

  wire not_1_out, not_2_out;

  S_R_Flip_Flop #(.Pre_Clr_Positions("LEGACY"), .NewFFLayout("false")) s_r_ff_1 (
    .S(in_1), .R(in_3), .Q(out_7), .Qn(out_9), .preset(in_1), .reset(in_3));  // open: clk
  D_Flip_Flop #(.Pre_Clr_Positions("LEGACY"), .NewFFLayout("false")) d_ff_1 (
    .D(in_5), .Q(out_11), .Qn(out_13), .preset(in_5), .reset(not_1_out));  // open: clk
  not not_1 (not_1_out, in_5);
  J_K_Flip_Flop #(.Pre_Clr_Positions("LEGACY"), .NewFFLayout("false")) j_k_ff_1 (
    .J(in_2), .K(in_4), .Q(out_8), .Qn(out_10), .preset(in_2), .reset(in_4));  // open: clk
  T_Flip_Flop #(.Pre_Clr_Positions("LEGACY"), .NewFFLayout("false")) t_ff_1 (
    .T(in_6), .Q(out_12), .Qn(out_14), .preset(in_6), .reset(not_2_out));  // open: clk
  not not_2 (not_2_out, in_6);
endmodule

module ROM (
  input  in_1,
  input  [1:0] in_2,
  output [1:0] out_3
);

  wire demultiplexer_1_out0, demultiplexer_1_out1, demultiplexer_1_out2, demultiplexer_1_out3,
       transistor_1_out, transistor_2_out, transistor_3_out, transistor_5_out;

  Demultiplexer #(.select(2), .enable("false")) demultiplexer_1 (
    .out0(demultiplexer_1_out0), .out1(demultiplexer_1_out1), .out2(demultiplexer_1_out2),
    .out3(demultiplexer_1_out3), .in(in_1), .sel(in_2));
  Pull_Resistor pull_resistor_1 (.node(out_3[1]));
  Transistor #(.\type ("n")) transistor_1 (
    .in(demultiplexer_1_out0), .out(transistor_1_out), .gate(demultiplexer_1_out0));
  Transistor #(.\type ("n")) transistor_2 (
    .in(demultiplexer_1_out0), .out(transistor_2_out), .gate(demultiplexer_1_out0));
  Transistor #(.\type ("n")) transistor_3 (
    .in(demultiplexer_1_out1), .out(transistor_3_out), .gate(demultiplexer_1_out1));
  Transistor #(.\type ("n")) transistor_4 (.in(demultiplexer_1_out1), .out(out_3[0]), .gate(demultiplexer_1_out1));
  Transistor #(.\type ("n")) transistor_5 (
    .in(demultiplexer_1_out2), .out(transistor_5_out), .gate(demultiplexer_1_out2));
  Transistor #(.\type ("n")) transistor_6 (.in(demultiplexer_1_out2), .out(out_3[1]), .gate(demultiplexer_1_out2));
  Transistor #(.\type ("n")) transistor_7 (.in(demultiplexer_1_out3), .out(out_3[0]), .gate(demultiplexer_1_out3));
  Transistor #(.\type ("n")) transistor_8 (.in(demultiplexer_1_out3), .out(out_3[1]), .gate(demultiplexer_1_out3));
  Pull_Resistor pull_resistor_2 (.node(out_3[0]));
  // also tied to GND on the sheet: {transistor_2_out, transistor_3_out, transistor_1_out, transistor_5_out}
endmodule

module RAM_1x1 (
  input  add,
  input  R_W,
  input  Clk,
  input  In,
  input  Clr,
  output out
);

  wire and_1_out, d_ff_1_q;

  and and_1 (and_1_out, add, R_W, Clk);
  D_Flip_Flop #(.Pre_Clr_Positions("LEGACY"), .NewFFLayout("false")) d_ff_1 (
    .clk(and_1_out), .D(In), .Q(d_ff_1_q), .reset(Clr));  // open: Qn, preset
  and and_2 (out, add, d_ff_1_q);
endmodule

module RAM_1x2 (
  input  add,
  input  R_W,
  input  clk,
  input  clr,
  input  in,
  input  in_2,
  output out,
  output out_2
);

  RAM_1x1 ram_1x1_1 (.R_W(R_W), .Clk(clk), .Clr(clr), .add(add), .out(out_2), .In(in_2));
  RAM_1x1 ram_1x1_2 (.R_W(R_W), .Clk(clk), .Clr(clr), .add(add), .out(out), .In(in));

  // Notes on the sheet:
  //   RAM 1x2
endmodule

module RAM_1x2b (
  input  in_1,
  input  in_2,
  input  in_3,
  input  in_4,
  input  [1:0] in_5,
  output [1:0] out_6
);

  RAM_1x2 ram_1x2_1 (
    .R_W(in_1), .clk(in_3), .clr(in_4), .add(in_2), .out(out_6[0]), .out_2(out_6[1]), .in(in_5[0]),
    .in_2(in_5[1]));
endmodule

module RAM_2x1 (
  input  R_W,
  input  add,
  input  clk,
  input  clr,
  input  in,
  output out
);

  wire demultiplexer_1_out0, demultiplexer_1_out1, ram_1x1_1_out, ram_1x1_2_out;

  RAM_1x1 ram_1x1_1 (.R_W(R_W), .Clk(clk), .Clr(clr), .add(demultiplexer_1_out0), .out(ram_1x1_1_out), .In(in));
  RAM_1x1 ram_1x1_2 (.R_W(R_W), .Clk(clk), .Clr(clr), .add(demultiplexer_1_out1), .out(ram_1x1_2_out), .In(in));
  Demultiplexer #(.enable("false")) demultiplexer_1 (
    .out0(demultiplexer_1_out0), .out1(demultiplexer_1_out1), .in(1'b1), .sel(add));
  Multiplexer #(.enable("false")) multiplexer_1 (.in0(ram_1x1_1_out), .in1(ram_1x1_2_out), .out(out), .sel(add));

  // Notes on the sheet:
  //   RAM 2x1
endmodule

module RAM_2x2 (
  input  add,
  input  R_W,
  input  [1:0] in,
  input  clk,
  input  clr,
  output [1:0] out
);

  wire demultiplexer_1_out0, demultiplexer_1_out1;
  wire [1:0] ram_1x2b_1_out_6, ram_1x2b_2_out_6;

  Demultiplexer #(.enable("false")) demultiplexer_1 (
    .out0(demultiplexer_1_out0), .out1(demultiplexer_1_out1), .in(1'b1), .sel(add));
  RAM_1x2b ram_1x2b_1 (
    .in_1(R_W), .in_3(clk), .in_4(clr), .in_2(demultiplexer_1_out0), .out_6(ram_1x2b_1_out_6), .in_5(in));
  RAM_1x2b ram_1x2b_2 (
    .in_1(R_W), .in_3(clk), .in_4(clr), .in_2(demultiplexer_1_out1), .out_6(ram_1x2b_2_out_6), .in_5(in));
  Multiplexer #(.width(2), .enable("false")) multiplexer_1 (
    .in0(ram_1x2b_1_out_6), .in1(ram_1x2b_2_out_6), .out(out), .sel(add));

  // Notes on the sheet:
  //   RAM 2x2
endmodule
