// Logisim project Sum-Sub.circ as structural Verilog: 1 circuit, main circuit main
module main (
  input  _0_Sum_1_Sub,
  input  in_2,
  input  in_3,
  input  in_4,
  output out_5,
  output out_6
);

  wire and_1_out, multiplexer_1_out, not_1_out, or_1_out, xnor_1_out, xor_1_out;

  Multiplexer #(.enable("false")) multiplexer_1 (
    .in0(in_2), .in1(not_1_out), .out(multiplexer_1_out), .sel(_0_Sum_1_Sub));
  not not_1 (not_1_out, in_2);
  and and_1 (and_1_out, in_3, in_4);
  or or_1 (or_1_out, in_3, in_4);
  xor xor_1 (xor_1_out, in_3, in_4);
  xnor xnor_1 (xnor_1_out, in_3, in_4);
  Multiplexer #(.enable("false")) multiplexer_2 (.in0(and_1_out), .in1(or_1_out), .out(out_5), .sel(multiplexer_1_out));
  Multiplexer #(.enable("false")) multiplexer_3 (.in0(xor_1_out), .in1(xnor_1_out), .out(out_6), .sel(in_2));
endmodule
