// Logisim project Sum-b.circ as structural Verilog: 1 circuit, main circuit main
module main (
  input  x,
  input  clr
);

  wire and_1_out, and_2_out, and_3_out, and_4_out, and_5_out, c_out, d_ff_1_qn, d_ff_2_qn, not_1_out,
       not_2_out, not_3_out, or_1_out, or_2_out;
  wire [1:0] d_ff_2_q;

  Button c (.out(c_out));
  not not_1 (not_1_out, c_out);
  and and_1 (and_1_out, not_2_out, d_ff_2_q[1]);
  not not_2 (not_2_out, c_out);
  D_Flip_Flop #(.Pre_Clr_Positions("LEGACY"), .NewFFLayout("false")) d_ff_1 (
    .clk(not_1_out), .D(or_1_out), .Q(d_ff_2_q[1]), .Qn(d_ff_1_qn), .reset(clr));  // open: preset
  or or_1 (or_1_out, and_1_out, and_3_out, and_2_out);
  and and_2 (and_2_out, d_ff_2_q[0], d_ff_1_qn);
  and and_3 (and_3_out, d_ff_2_qn, d_ff_2_q[1]);
  or or_2 (or_2_out, and_4_out, and_5_out);
  and and_4 (and_4_out, not_3_out, d_ff_2_q[0]);
  not not_3 (not_3_out, c_out);
  // Probe on d_ff_2_q[1]
  // Probe on d_ff_2_q[0]
  D_Flip_Flop #(.Pre_Clr_Positions("LEGACY"), .NewFFLayout("false")) d_ff_2 (
    .clk(not_1_out), .D(or_2_out), .Q(d_ff_2_q[0]), .Qn(d_ff_2_qn), .reset(clr));  // open: preset
  and and_5 (and_5_out, c_out, d_ff_2_qn);
  // Probe on d_ff_2_q

  // Notes on the sheet:
  //   ac'+ab'+a'bc
  //   bc'+b'c
endmodule
