// Logisim project Sum.circ as structural Verilog
module Multi (
  input  in_1,
  input  in_2,
  input  in_3,
  output out_4
);

  wire and_1_out, and_2_out, not_1_out;

  not not_1 (not_1_out, in_3);
  and and_1 (and_1_out, in_1, not_1_out);
  or or_1 (out_4, and_1_out, and_2_out);
  and and_2 (and_2_out, in_2, in_3);
endmodule

module Multi_3bit (
  input  [7:0] in_1,
  input  [2:0] Key,
  output out_3
);

  wire multi_1_out_4, multi_2_out_4, multi_3_out_4, multi_4_out_4, multi_5_out_4, multi_7_out_4;

  Multi multi_1 (.in_1(in_1[0]), .in_2(in_1[1]), .out_4(multi_1_out_4), .in_3(Key[0]));
  Multi multi_2 (.in_1(in_1[2]), .in_2(in_1[3]), .out_4(multi_2_out_4), .in_3(Key[0]));
  Multi multi_3 (.in_1(in_1[4]), .in_2(in_1[5]), .out_4(multi_3_out_4), .in_3(Key[0]));
  Multi multi_4 (.in_1(in_1[6]), .in_2(in_1[7]), .out_4(multi_4_out_4), .in_3(Key[0]));
  Multi multi_5 (.in_1(multi_1_out_4), .in_2(multi_2_out_4), .out_4(multi_5_out_4), .in_3(Key[1]));
  Multi multi_6 (.in_1(multi_5_out_4), .in_2(multi_7_out_4), .out_4(out_3), .in_3(Key[2]));
  Multi multi_7 (.in_1(multi_3_out_4), .in_2(multi_4_out_4), .out_4(multi_7_out_4), .in_3(Key[1]));
endmodule

module Half_sum (
  input  A,
  input  B,
  output s1,
  output s0
);

  wire not_1_out, or_1_out;

  or or_1 (or_1_out, B, A);
  and and_1 (s1, B, A);
  and and_2 (s0, or_1_out, not_1_out);
  not not_1 (not_1_out, s1);
endmodule

module Half_diff (
  input  A,
  input  B,
  output out_3,
  output out_4
);

  wire not_1_out;

  not not_1 (not_1_out, A);
  xor xor_1 (out_3, A, B);
  and and_1 (out_4, B, not_1_out);
endmodule

module Full_sum (
  input  in_1,
  input  in_2,
  input  in_3,
  output out_4,
  output out_5
);

  wire half_sum_1_s0, half_sum_1_s1, half_sum_2_s1;

  Half_sum half_sum_1 (.A(in_2), .B(in_1), .s1(half_sum_1_s1), .s0(half_sum_1_s0));
  Half_sum half_sum_2 (.A(half_sum_1_s0), .B(in_3), .s1(half_sum_2_s1), .s0(out_4));
  Half_sum half_sum_3 (.A(half_sum_2_s1), .B(half_sum_1_s1), .s0(out_5));  // open: s1
endmodule

module Full_diff (
  input  in_1,
  input  in_2,
  input  in_3,
  output out_4,
  output out_5
);

  wire and_1_out, or_1_out, xnor_1_out, xor_1_out;

  or or_1 (or_1_out, in_2, in_3);
  and and_1 (and_1_out, in_2, in_3);
  xor xor_1 (xor_1_out, in_2, in_3);
  Multi multi_1 (.in_1(xor_1_out), .in_2(xnor_1_out), .out_4(out_4), .in_3(in_1));
  xnor xnor_1 (xnor_1_out, in_2, in_3);
  Multi multi_2 (.in_1(or_1_out), .in_2(and_1_out), .out_4(out_5), .in_3(in_1));
endmodule

module Bigger_Smaller (
  input  A,
  input  B,
  input  _0___A___B___1___B___A,
  output S
);

  wire and_1_out, and_2_out, not_1_out, not_2_out;

  not not_1 (not_1_out, B);
  not not_2 (not_2_out, A);
  and and_1 (and_1_out, not_1_out, A);
  and and_2 (and_2_out, B, not_2_out);
  Multi multi_1 (.in_1(and_1_out), .in_2(and_2_out), .out_4(S), .in_3(_0___A___B___1___B___A));
endmodule

module LU (
  input  A,
  input  B,
  input  [2:0] in_3,
  output S
);

  wire [7:0] not_1_out;

  not not_1 (not_1_out[0], B);
  not not_2 (not_1_out[1], A);
  and and_1 (not_1_out[2], B, A);
  nand nand_1 (not_1_out[3], B, A);
  or or_1 (not_1_out[4], B, A);
  nor nor_1 (not_1_out[5], B, A);
  xor xor_1 (not_1_out[6], B, A);
  xnor xnor_1 (not_1_out[7], B, A);
  Multi_3bit multi_3bit_1 (.in_1(not_1_out), .out_3(S), .Key(in_3));
endmodule

module a (
  input  in_1,
  input  in_2,
  input  in_3,
  output out_4,
  output out_5
);

  wire and_1_out, and_2_out, not_1_out, not_2_out;

  not not_1 (not_1_out, in_1);
  xor xor_1 (in_3, in_1, in_2);
  and and_1 (and_1_out, in_2, not_1_out);
  xor xor_2 (out_4, in_3, in_3);
  and and_2 (and_2_out, in_3, not_2_out);
  not not_2 (not_2_out, in_3);
  or or_1 (out_5, and_2_out, and_1_out);
endmodule

module fasf (
  input  in_1,
  input  in_2,
  input  in_3,
  input  in_4,
  input  in_5,
  input  in_6,
  input  in_7,
  input  in_8
);

  wire or_1_out, or_2_out, xor_1_out, xor_2_out;

  or or_1 (or_1_out, in_1, in_3);
  or or_2 (or_2_out, in_5, in_7);
  // AND_Gate and_1 has open pins: in0=or_1_out, in1=or_2_out, out=open
  xor xor_1 (xor_1_out, in_2, in_4);
  // AND_Gate and_2 has open pins: in0=xor_1_out, in1=xor_2_out, out=open
  xor xor_2 (xor_2_out, in_6, in_8);
endmodule
